// Logisim project pcb_computer.circ as structural Verilog: 10 circuits, main circuit main
module main (
);

  wire Clk, microcode_1_a, microcode_1_b, nand_1_out;
  wire [7:0] Bus8, programcounter_1_addressout, programcounter_1_addressout_2, ram_idt7134_1_dataoutr;
  wire [15:0] ALow_dataout, memoryhelper_1_ramaddress;

  Clock clock_1 (.out(Clk));
  // Probe on Bus8
  Microcode microcode_1 (.NotClear(1'b1), .Clock(Clk), .A(microcode_1_a), .B(microcode_1_b));
  nand nand_1 (nand_1_out, microcode_1_a, microcode_1_b);
  Register8 IRHigh (.Clock(Clk), .NotLoad(1'b0), .NotEnable(1'b1), .BusIn(Bus8), .BusOut(Bus8));  // open: DataOut
  Register8 IRLow (.Clock(Clk), .NotLoad(1'b1), .NotEnable(1'b1), .BusIn(Bus8), .BusOut(Bus8));  // open: DataOut
  Register8 AHigh (
    .Clock(Clk), .NotLoad(1'b1), .NotEnable(1'b1), .BusIn(Bus8), .BusOut(Bus8), .DataOut(ALow_dataout[15:8]));
  Register8 ALow (
    .Clock(Clk), .NotLoad(1'b1), .NotEnable(1'b1), .BusIn(Bus8), .BusOut(Bus8), .DataOut(ALow_dataout[7:0]));
  Register8 B (.Clock(Clk), .NotLoad(1'b1), .NotEnable(1'b1), .BusIn(Bus8), .BusOut(Bus8));  // open: DataOut
  Register8 C (.Clock(Clk), .NotLoad(1'b1), .NotEnable(1'b1), .BusIn(Bus8), .BusOut(Bus8));  // open: DataOut
  ProgramCounter programcounter_1 (
    .Clock(Clk), .NotClear(1'b1), .NotLoad(1'b1), .Count(1'b1), .AddressIn(ALow_dataout),
    .AddressOut({programcounter_1_addressout_2, programcounter_1_addressout}));
  MemoryHelper memoryhelper_1 (
    .NotEnablePC(1'b0), .PCHigh(programcounter_1_addressout_2), .PCLow(programcounter_1_addressout),
    .NotEnableA(1'b1), .AHigh(ALow_dataout[15:8]), .ALow(ALow_dataout[7:0]),
    .RAMAddress(memoryhelper_1_ramaddress));
  // Probe on {programcounter_1_addressout_2, programcounter_1_addressout}
  // Probe on memoryhelper_1_ramaddress[1:0]
  RAM_IDT7134 ram_idt7134_1 (
    .Clock(Clk), .DataInL(Bus8), .NotWriteRamL(1'b1), .AddressL(memoryhelper_1_ramaddress[1:0]),
    .AddressR(2'b00), .NotOutputEnableL(1'b0), .NotOutputEnableR(1'b0), .DataOutL(Bus8),
    .DataOutR(ram_idt7134_1_dataoutr));
  // Probe on Bus8
  // Probe on ram_idt7134_1_dataoutr
endmodule

module OctalTransceiver74245 (
  input  [7:0] B_in,
  input  NotEnable,
  input  Dir,
  input  [7:0] A_in,
  output [7:0] B_Out,
  output [7:0] A_out
);

  wire and_1_out, and_2_out, not_1_out, not_2_out, not_3_out;

  not not_1 (not_1_out, Dir);
  not not_2 (not_2_out, NotEnable);
  and and_1 (and_1_out, not_1_out, not_2_out);
  and and_2 (and_2_out, Dir, not_3_out);
  not not_3 (not_3_out, NotEnable);
  assign A_out[0] = and_1_out ? B_in[0] : 1'bz;  // Controlled_Buffer controlled_buffer_1
  assign A_out[1] = and_1_out ? B_in[1] : 1'bz;  // Controlled_Buffer controlled_buffer_2
  assign B_Out[0] = and_2_out ? A_in[0] : 1'bz;  // Controlled_Buffer controlled_buffer_3
  assign B_Out[1] = and_2_out ? A_in[1] : 1'bz;  // Controlled_Buffer controlled_buffer_4
  assign A_out[2] = and_1_out ? B_in[2] : 1'bz;  // Controlled_Buffer controlled_buffer_5
  assign A_out[3] = and_1_out ? B_in[3] : 1'bz;  // Controlled_Buffer controlled_buffer_6
  assign B_Out[2] = and_2_out ? A_in[2] : 1'bz;  // Controlled_Buffer controlled_buffer_7
  assign B_Out[3] = and_2_out ? A_in[3] : 1'bz;  // Controlled_Buffer controlled_buffer_8
  assign A_out[4] = and_1_out ? B_in[4] : 1'bz;  // Controlled_Buffer controlled_buffer_9
  assign A_out[5] = and_1_out ? B_in[5] : 1'bz;  // Controlled_Buffer controlled_buffer_10
  assign B_Out[4] = and_2_out ? A_in[4] : 1'bz;  // Controlled_Buffer controlled_buffer_11
  assign B_Out[5] = and_2_out ? A_in[5] : 1'bz;  // Controlled_Buffer controlled_buffer_12
  assign A_out[6] = and_1_out ? B_in[6] : 1'bz;  // Controlled_Buffer controlled_buffer_13
  assign A_out[7] = and_1_out ? B_in[7] : 1'bz;  // Controlled_Buffer controlled_buffer_14
  assign B_Out[6] = and_2_out ? A_in[6] : 1'bz;  // Controlled_Buffer controlled_buffer_15
  assign B_Out[7] = and_2_out ? A_in[7] : 1'bz;  // Controlled_Buffer controlled_buffer_16
endmodule

module Register8 (
  input  Clock,
  input  NotLoad,
  input  NotEnable,
  input  [7:0] BusIn,
  output [7:0] BusOut,
  output [7:0] DataOut
);

  OctalTransceiver74245 octaltransceiver74245_1 (
    .B_Out(BusOut), .A_out(DataOut), .Dir(1'b1), .NotEnable(NotEnable), .B_in(BusOut), .A_in(DataOut));
  _74377 #(.ShowInternalStructure("true")) u_74377_1 (
    .pin1(NotLoad), .pin2(DataOut[0]), .pin3(BusIn[0]), .pin4(BusIn[1]), .pin5(DataOut[1]),
    .pin6(DataOut[2]), .pin7(BusIn[2]), .pin8(BusIn[3]), .pin9(DataOut[3]), .pin19(DataOut[7]),
    .pin18(BusIn[7]), .pin17(BusIn[6]), .pin16(DataOut[6]), .pin15(DataOut[5]), .pin14(BusIn[5]),
    .pin13(BusIn[4]), .pin12(DataOut[4]), .pin11(Clock));
endmodule

module ProgramCounter (
  input  Clock,
  input  NotClear,
  input  NotLoad,
  input  Count,
  input  [15:0] AddressIn,
  output [15:0] AddressOut
);

  wire n74161_1_pin15, n74161_2_pin15, n74161_3_pin15;

  _74161 #(.ShowInternalStructure("true")) u_74161_1 (
    .pin1(NotClear), .pin2(Clock), .pin3(AddressIn[0]), .pin4(AddressIn[1]), .pin5(AddressIn[2]),
    .pin6(AddressIn[3]), .pin7(Count), .pin15(n74161_1_pin15), .pin14(AddressOut[0]), .pin13(AddressOut[1]),
    .pin12(AddressOut[2]), .pin11(AddressOut[3]), .pin10(NotLoad), .pin9(NotLoad));
  _74161 #(.ShowInternalStructure("true")) u_74161_2 (
    .pin1(NotClear), .pin2(Clock), .pin3(AddressIn[4]), .pin4(AddressIn[5]), .pin5(AddressIn[6]),
    .pin6(AddressIn[7]), .pin7(Count), .pin15(n74161_2_pin15), .pin14(AddressOut[4]), .pin13(AddressOut[5]),
    .pin12(AddressOut[6]), .pin11(AddressOut[7]), .pin10(n74161_1_pin15), .pin9(NotLoad));
  _74161 #(.ShowInternalStructure("true")) u_74161_3 (
    .pin1(NotClear), .pin2(Clock), .pin3(AddressIn[8]), .pin4(AddressIn[9]), .pin5(AddressIn[10]),
    .pin6(AddressIn[11]), .pin7(Count), .pin15(n74161_3_pin15), .pin14(AddressOut[8]), .pin13(AddressOut[9]),
    .pin12(AddressOut[10]), .pin11(AddressOut[11]), .pin10(n74161_2_pin15), .pin9(NotLoad));
  _74161 #(.ShowInternalStructure("true")) u_74161_4 (
    .pin1(NotClear), .pin2(Clock), .pin3(AddressIn[12]), .pin4(AddressIn[13]), .pin5(AddressIn[14]),
    .pin6(AddressIn[15]), .pin7(Count), .pin14(AddressOut[12]), .pin13(AddressOut[13]),
    .pin12(AddressOut[14]), .pin11(AddressOut[15]), .pin10(n74161_3_pin15), .pin9(NotLoad));  // open: pin15

  // Other names for the same wires on the sheet: Clk = Clock; nClr = NotClear; nLD = NotLoad
endmodule

module Bus16 (
  input  NotEnablePC,
  input  [7:0] PCHigh,
  input  [7:0] PCLow,
  input  NotEnableA,
  input  [7:0] AHigh,
  input  [7:0] ALow,
  output [15:0] RAMAddress
);

  OctalTransceiver74245 octaltransceiver74245_1 (
    .B_Out(PCHigh), .A_out(RAMAddress[15:8]), .Dir(1'b0), .NotEnable(NotEnablePC), .B_in(PCHigh),
    .A_in(RAMAddress[15:8]));
  OctalTransceiver74245 octaltransceiver74245_2 (
    .B_Out(PCLow), .A_out(RAMAddress[7:0]), .Dir(1'b0), .NotEnable(NotEnablePC), .B_in(PCLow),
    .A_in(RAMAddress[7:0]));
  OctalTransceiver74245 octaltransceiver74245_3 (
    .B_Out(AHigh), .A_out(RAMAddress[15:8]), .Dir(1'b0), .NotEnable(NotEnableA), .B_in(AHigh),
    .A_in(RAMAddress[15:8]));
  OctalTransceiver74245 octaltransceiver74245_4 (
    .B_Out(ALow), .A_out(RAMAddress[7:0]), .Dir(1'b0), .NotEnable(NotEnableA), .B_in(ALow),
    .A_in(RAMAddress[7:0]));
endmodule

module MemoryHelper (
  input  NotEnablePC,
  input  [7:0] PCHigh,
  input  [7:0] PCLow,
  input  NotEnableA,
  input  [7:0] AHigh,
  input  [7:0] ALow,
  output [15:0] RAMAddress
);

  OctalTransceiver74245 octaltransceiver74245_1 (
    .B_Out(PCHigh), .A_out(RAMAddress[15:8]), .Dir(1'b0), .NotEnable(NotEnablePC), .B_in(PCHigh),
    .A_in(RAMAddress[15:8]));
  OctalTransceiver74245 octaltransceiver74245_2 (
    .B_Out(PCLow), .A_out(RAMAddress[7:0]), .Dir(1'b0), .NotEnable(NotEnablePC), .B_in(PCLow),
    .A_in(RAMAddress[7:0]));
  OctalTransceiver74245 octaltransceiver74245_3 (
    .B_Out(AHigh), .A_out(RAMAddress[15:8]), .Dir(1'b0), .NotEnable(NotEnableA), .B_in(AHigh),
    .A_in(RAMAddress[15:8]));
  OctalTransceiver74245 octaltransceiver74245_4 (
    .B_Out(ALow), .A_out(RAMAddress[7:0]), .Dir(1'b0), .NotEnable(NotEnableA), .B_in(ALow),
    .A_in(RAMAddress[7:0]));
endmodule

module Microcode (
  input  NotClear,
  input  Clock,
  output A,
  output B
);

  wire n74161_1_pin7;

  _74161 #(.ShowInternalStructure("true")) u_74161_1 (
    .pin1(NotClear), .pin2(Clock), .pin7(n74161_1_pin7), .pin14(A), .pin13(B), .pin10(n74161_1_pin7),
    .pin9(n74161_1_pin7));  // open: pin3, pin4, pin5, pin6, pin15, pin12, pin11
  // also tied to VCC on the sheet: n74161_1_pin7
endmodule

module RAM_2 (
  input  Clock,
  input  [7:0] DataInL,
  input  WriteL,
  input  AddressL,
  input  AddressR,
  output [7:0] DataOutR,
  output [7:0] DataOutL
);

  wire decoder_1_out0, decoder_1_out1, not_1_out;
  wire [7:0] multiplexer_1_out, register_1_q, register_2_q;

  Decoder decoder_1 (.out0(decoder_1_out0), .out1(decoder_1_out1), .sel(AddressL), .en(WriteL));
  Register register_1 (.D(DataInL), .en(decoder_1_out0), .clk(Clock), .Q(register_1_q), .clr(1'b0));
  Register register_2 (.D(DataInL), .en(decoder_1_out1), .clk(Clock), .Q(register_2_q), .clr(1'b0));
  Multiplexer #(.width(8)) multiplexer_1 (
    .in0(register_1_q), .in1(register_2_q), .out(multiplexer_1_out), .sel(AddressL));
  Multiplexer #(.width(8)) multiplexer_2 (.in0(register_1_q), .in1(register_2_q), .out(DataOutR), .sel(AddressR));
  assign DataOutL = not_1_out ? multiplexer_1_out : 8'bz;  // Controlled_Buffer controlled_buffer_1
  not not_1 (not_1_out, WriteL);
endmodule

module RAM_4 (
  input  Clock,
  input  [7:0] DataInL,
  input  NotWriteL,
  input  [1:0] AddressL,
  input  [1:0] AddressR,
  output [7:0] DataOutL,
  output [7:0] DataOutR
);

  wire decoder_1_out0, decoder_1_out1, not_1_out, undriven, undriven_2;
  wire [7:0] multiplexer_1_out, ram_2_1_dataoutl, ram_2_1_dataoutr, ram_2_2_dataoutl, ram_2_2_dataoutr;

  not not_1 (not_1_out, NotWriteL);
  Decoder decoder_1 (.out0(decoder_1_out0), .out1(decoder_1_out1), .sel(AddressL[1]), .en(not_1_out));
  RAM_2 ram_2_1 (
    .Clock(Clock), .DataInL(DataInL), .WriteL(decoder_1_out0), .AddressL(AddressL[0]),
    .AddressR(AddressR[0]), .DataOutR(ram_2_1_dataoutr), .DataOutL(ram_2_1_dataoutl));
  RAM_2 ram_2_2 (
    .Clock(Clock), .DataInL(DataInL), .WriteL(decoder_1_out1), .AddressL(AddressL[0]),
    .AddressR(AddressR[0]), .DataOutR(ram_2_2_dataoutr), .DataOutL(ram_2_2_dataoutl));
  Multiplexer #(.width(8)) multiplexer_1 (
    .in0(ram_2_1_dataoutl), .in1(ram_2_2_dataoutl), .out(multiplexer_1_out), .sel(AddressL[1]));
  Multiplexer #(.width(8)) multiplexer_2 (
    .in0(ram_2_1_dataoutr), .in1(ram_2_2_dataoutr), .out(DataOutR), .sel(AddressR[1]));
  assign DataOutL = NotWriteL ? multiplexer_1_out : 8'bz;  // Controlled_Buffer controlled_buffer_1
  // Probe on nothing
  // Probe on undriven
  // Probe on undriven
  // Probe on undriven_2
  // Probe on undriven_2
endmodule

module RAM_IDT7134 (
  input  Clock,
  input  [7:0] DataInL,
  input  NotWriteRamL,
  input  [1:0] AddressL,
  input  [1:0] AddressR,
  input  NotOutputEnableL,
  input  NotOutputEnableR,
  output [7:0] DataOutL,
  output [7:0] DataOutR
);

  wire not_1_out, not_2_out;
  wire [7:0] ram_4_1_dataoutl, ram_4_1_dataoutr;

  RAM_4 ram_4_1 (
    .Clock(Clock), .DataInL(DataInL), .NotWriteL(NotWriteRamL), .AddressL(AddressL), .AddressR(AddressR),
    .DataOutL(ram_4_1_dataoutl), .DataOutR(ram_4_1_dataoutr));
  assign DataOutL = not_1_out ? ram_4_1_dataoutl : 8'bz;  // Controlled_Buffer controlled_buffer_1
  not not_1 (not_1_out, NotOutputEnableL);
  assign DataOutR = not_2_out ? ram_4_1_dataoutr : 8'bz;  // Controlled_Buffer controlled_buffer_2
  not not_2 (not_2_out, NotOutputEnableR);
endmodule
